// Logisim project 4-Bit Asynchronous (Ripple) Counter.circ as structural Verilog: 1 circuit, main circuit main
module main (
  input  Reset,
  input  in_2,
  output _0,
  output _1,
  output _2,
  output _3
);

  wire clock_1_out, j_k_ff_1_qn, j_k_ff_2_qn, j_k_ff_3_qn;

  Clock clock_1 (.out(clock_1_out));
  J_K_Flip_Flop j_k_ff_1 (
    .J(in_2), .clk(clock_1_out), .K(in_2), .Q(_0), .Qn(j_k_ff_1_qn), .reset(Reset));  // open: preset, en
  J_K_Flip_Flop j_k_ff_2 (
    .J(in_2), .clk(j_k_ff_1_qn), .K(in_2), .Q(_1), .Qn(j_k_ff_2_qn), .reset(Reset));  // open: preset, en
  J_K_Flip_Flop j_k_ff_3 (
    .J(in_2), .clk(j_k_ff_2_qn), .K(in_2), .Q(_2), .Qn(j_k_ff_3_qn), .reset(Reset));  // open: preset, en
  J_K_Flip_Flop j_k_ff_4 (.J(in_2), .clk(j_k_ff_3_qn), .K(in_2), .Q(_3), .reset(Reset));  // open: Qn, preset, en

  // Notes on the sheet:
  //   CLK
  //   4-Bit Asynchronous (Ripple) Counter 
endmodule
