// Logisim project 4-bit Synchronous Counter.circ as structural Verilog: 1 circuit, main circuit main
module main (
  input  A,
  output _2,
  output _3,
  output _0,
  output _1
);

  wire and_1_out, and_2_out, clock_1_out;

  Clock clock_1 (.out(clock_1_out));
  J_K_Flip_Flop j_k_ff_1 (.J(A), .clk(clock_1_out), .K(A), .Q(_0));  // open: Qn, preset, en, reset
  J_K_Flip_Flop j_k_ff_2 (.J(_0), .clk(clock_1_out), .K(_0), .Q(_1));  // open: Qn, preset, en, reset
  and and_1 (and_1_out, _0, _1);
  and and_2 (and_2_out, and_1_out, _2);
  J_K_Flip_Flop j_k_ff_3 (.J(and_1_out), .clk(clock_1_out), .K(and_1_out), .Q(_2));  // open: Qn, preset, en, reset
  J_K_Flip_Flop j_k_ff_4 (.J(and_2_out), .clk(clock_1_out), .K(and_2_out), .Q(_3));  // open: Qn, preset, en, reset

  // Notes on the sheet:
  //   CLK
  //   4-Bit Synchronous Counter
endmodule
