// Logisim project D FlipFlop.circ as structural Verilog: 1 circuit, main circuit main
module main (
  input  A,
  input  in_2,
  output OUTPUT_1,
  output OUTPUT_2
);

  wire and_1_out, and_2_out, not_1_out;

  not not_1 (not_1_out, A);
  and and_1 (and_1_out, A, A, in_2);
  and and_2 (and_2_out, in_2, not_1_out);
  nor nor_1 (OUTPUT_1, and_1_out, OUTPUT_2);
  nor nor_2 (OUTPUT_2, OUTPUT_1, and_2_out);

  // Notes on the sheet:
  //   D FlipFloP
endmodule
