// Logisim project Register File of 4 Registers.circ as structural Verilog: 2 circuits, main circuit 4 bit circuit
// 4 Bit register file
module _4_bit_circuit (
  input  [1:0] Write_Register,
  input  [1:0] Read_register_1,
  input  [1:0] Read_register_2,
  input  [3:0] Write_data,
  input  Input,
  input  clock,
  output [3:0] Read_Data_1,
  output [3:0] Read_Data_2
);

  wire and_1_out, and_2_out, and_3_out, and_4_out, decoder_1_out0, decoder_1_out1, decoder_1_out2,
       decoder_1_out3;
  wire [3:0] register_1_q, register_2_q, register_3_q, register_4_q;

  Decoder #(.select(2)) decoder_1 (
    .out0(decoder_1_out0), .out1(decoder_1_out1), .out2(decoder_1_out2), .out3(decoder_1_out3),
    .sel(Write_Register));  // open: en
  and and_1 (and_1_out, decoder_1_out0, Input);
  and and_2 (and_2_out, decoder_1_out1, Input);
  Register #(.width(4)) register_1 (.D(Write_data), .Q(register_1_q), .clk(clock), .clr(and_1_out));  // open: en
  Register #(.width(4)) register_2 (.D(Write_data), .Q(register_2_q), .clk(clock), .clr(and_2_out));  // open: en
  and and_3 (and_3_out, decoder_1_out2, Input);
  and and_4 (and_4_out, decoder_1_out3, Input);
  Register #(.width(4)) register_3 (.D(Write_data), .Q(register_3_q), .clk(clock), .clr(and_3_out));  // open: en
  Register #(.width(4)) register_4 (.D(Write_data), .Q(register_4_q), .clk(clock), .clr(and_4_out));  // open: en
  Multiplexer #(.select(2), .width(4)) multiplexer_1 (
    .in0(register_1_q), .in1(register_2_q), .in2(register_3_q), .in3(register_4_q), .out(Read_Data_1),
    .sel(Read_register_1));  // open: en
  Multiplexer #(.select(2), .width(4)) multiplexer_2 (
    .in0(register_1_q), .in1(register_2_q), .in2(register_3_q), .in3(register_4_q), .out(Read_Data_2),
    .sel(Read_register_2));  // open: en

  // Notes on the sheet:
  //   Register File of 4 Registers
endmodule

module main (
  input  [1:0] Read_register_1,
  input  [1:0] Read_register_2,
  input  [1:0] Write_register,
  input  [3:0] Writedata,
  input  in_5,
  output [3:0] Read_data_2,
  output [3:0] Read_data_1
);

  wire n4_bit_circuit_1_p6;

  // _4_bit_circuit 4_bit_circuit_1: pin names not known; wires that end beside it: Read_register_1, Read_register_2, Write_register, Writedata, in_5, n4_bit_circuit_1_p6, Read_data_2, Read_data_1
  Clock clock_1 (.out(n4_bit_circuit_1_p6));
endmodule
