// Logisim project SR FlipFlop.circ as structural Verilog: 1 circuit, main circuit main
module main (
  input  A,
  input  C,
  input  B,
  output OUTPUT_1,
  output OUTPUT_2
);

  wire and_1_out, and_2_out;

  and and_1 (and_1_out, A, A, C);
  and and_2 (and_2_out, C, B);
  nor nor_1 (OUTPUT_1, and_1_out, OUTPUT_2);
  nor nor_2 (OUTPUT_2, OUTPUT_1, and_2_out);

  // Notes on the sheet:
  //   SR FlipFlop
endmodule
