// Logisim project T FlipFlop.circ as structural Verilog: 1 circuit, main circuit main
module main (
  input  A,
  output Output_1,
  output Output_2
);

  wire and_1_out, and_2_out, and_3_out, clock_1_out, nand_1_out, nor_1_out, nor_2_out, not_1_out;

  Clock clock_1 (.out(clock_1_out));
  nand nand_1 (nand_1_out, Output_1, A, clock_1_out);
  and and_1 (and_1_out, clock_1_out, A, Output_2);
  not not_1 (not_1_out, clock_1_out);
  nor nor_1 (nor_1_out, nand_1_out, nor_2_out);
  nor nor_2 (nor_2_out, nor_1_out, and_1_out);
  and and_2 (and_2_out, nor_1_out, nor_1_out, not_1_out);
  and and_3 (and_3_out, not_1_out, nor_2_out);
  nor nor_3 (Output_1, and_2_out, Output_2);
  nor nor_4 (Output_2, Output_1, and_3_out);

  // Notes on the sheet:
  //   T Flip-Flop
endmodule
